# Fritzing sketch BoilerMonitoring (saved by Fritzing 0.8.7b)
circuit board: 6.9215cm x 5.33756cm
breadboards: 1

parts:
  Boiler_ModBus_Interface = Netduino Plus
  A_GND_B = screw terminal, 3 pins
  J2 = female pin header, 4 pins [form="♀ (female)"]
  J3 = female pin header, 4 pins [form="♀ (female)"]
  PCB1 = Arduino Shield PCB  # not connected

nets:
  N1: Boiler_ModBus_Interface.GND, A_GND_B.pin2, J2.pin4
  N2: Boiler_ModBus_Interface.D3_TX1, J3.pin3
  N3: Boiler_ModBus_Interface.D2_RX1, J3.pin2
  N4: Boiler_ModBus_Interface.D1_TX0, J3.pin1
  N5: Boiler_ModBus_Interface.D0_RX0, J3.pin4
  N6: Boiler_ModBus_Interface.+5V, J2.pin1
  N7: A_GND_B.pin1, J2.pin2
  N8: A_GND_B.pin3, J2.pin3

custom parts:
  Arduino Shield PCB: Plain PCB Shaped to fit an Arduino "Shield"
