# Fritzing sketch PerimeterMonitoring (saved by Fritzing 0.8.7b)
circuit board: 6.9215cm x 5.33756cm
breadboards: 1

parts:
  Netduino1 = Netduino Plus
  J1 = screw terminal, 14 pins
  J2 = screw terminal, 14 pins
  R1 = Resistor [tolerance=±5% resistance=10k package=THT]
  R2 = Resistor [tolerance=±5% resistance=10k package=THT]
  R3 = Resistor [tolerance=±5% resistance=10k package=THT]
  R4 = Resistor [tolerance=±5% resistance=10k package=THT]
  R5 = Resistor [tolerance=±5% resistance=10k package=THT]
  R6 = Resistor [tolerance=±5% resistance=10k package=THT]
  R7 = Resistor [tolerance=±5% resistance=10k package=THT]
  R8 = Resistor [tolerance=±5% resistance=10k package=THT]
  R9 = Resistor [tolerance=±5% resistance=10k package=THT]
  R10 = Resistor [tolerance=±5% resistance=10k package=THT]
  R11 = Resistor [tolerance=±5% resistance=10k package=THT]
  R12 = Resistor [tolerance=±5% resistance=10k package=THT]
  R13 = Resistor [tolerance=±5% resistance=10k package=THT]
  R14 = Resistor [tolerance=±5% resistance=10k package=THT]
  PCB1 = Arduino Shield PCB  # not connected

nets:
  N1: Netduino1.GND, J1.pin2, J1.pin4, J1.pin6, J1.pin8, J1.pin10, J1.pin12, J1.pin14, J2.pin2, J2.pin4, J2.pin6, J2.pin8, J2.pin10, J2.pin12, J2.pin14
  N2: Netduino1.D13_SPCK, J1.pin13, R7.Pin_1
  N3: Netduino1.D12_MISO, J1.pin11, R6.Pin_1
  N4: Netduino1.D11_MOSI, J1.pin9, R5.Pin_1
  N5: Netduino1.D10_PWM3, J1.pin7, R4.Pin_1
  N6: Netduino1.D9_PWM2, J1.pin5, R3.Pin_1
  N7: Netduino1.D8_CTS1, J1.pin3, R2.Pin_1
  N8: Netduino1.D7_RTS1, J1.pin1, R1.Pin_1
  N9: Netduino1.D6_PWM1, J2.pin1, R8.Pin_1
  N10: Netduino1.D5_PWM0, J2.pin3, R9.Pin_1
  N11: Netduino1.D4_CS0, J2.pin5, R10.Pin_1
  N12: Netduino1.D3_TX1, J2.pin7, R11.Pin_1
  N13: Netduino1.D2_RX1, J2.pin9, R12.Pin_1
  N14: Netduino1.D1_TX0, J2.pin11, R13.Pin_1
  N15: Netduino1.D0_RX0, J2.pin13, R14.Pin_1
  N16: Netduino1.+5V, R1.Pin_0, R2.Pin_0, R3.Pin_0, R4.Pin_0, R5.Pin_0, R6.Pin_0, R7.Pin_0, R8.Pin_0, R9.Pin_0, R10.Pin_0, R11.Pin_0, R12.Pin_0, R13.Pin_0, R14.Pin_0

notes:
  Gnd 13 Gnd 12 Gnd 11 Gnd 10 Gnd 09 Gnd 08 Gnd 07
  Gnd 00 Gnd 01 Gnd 02 Gnd 03 Gnd 04 Gnd 05 Gnd 06

custom parts:
  Arduino Shield PCB: Plain PCB Shaped to fit an Arduino "Shield"
