# Fritzing sketch Propane (saved by Fritzing 0.8.7b)
circuit board: 6.9215cm x 5.33756cm
breadboards: 1

parts:
  Propane_Tank_Monitor = Netduino Plus
  LPG_(Propane)_Sensor = GAS_SENSOR [package=mq-3]
  220Ω = Resistor [tolerance=±5% resistance=220 package=THT]
  220Ω_2 = Resistor [tolerance=±5% resistance=220 package=THT]
  220Ω_3 = Resistor [tolerance=±5% resistance=220 package=THT]
  10kΩ = Resistor [tolerance=±5% resistance=10k package=THT]
  Level_Meter = Screw terminal - 2 pins [package=THT]
  Status = RGB LED (com. anode, rbg) [package="5 mm [THT]"]
  PCB1 = Arduino Shield PCB [sticky=true]  # not connected
  10kΩ_2 = Trimmer Potentiometer [maximum_resistance=10kΩ package=THT]

nets:
  N1: Propane_Tank_Monitor.D6_PWM1, 220Ω_2.Pin_0
  N2: Propane_Tank_Monitor.D5_PWM0, 220Ω.Pin_0
  N3: Propane_Tank_Monitor.D4_CS0, 220Ω_3.Pin_0
  N4: Propane_Tank_Monitor.3V3, 10kΩ.Pin_1
  N5: Propane_Tank_Monitor.+5V, LPG_(Propane)_Sensor.H2
  N6: Propane_Tank_Monitor.GND, LPG_(Propane)_Sensor.H1, Level_Meter.pin2, Status.common_anode, 10kΩ_2.wiper, 10kΩ_2.leg2
  N7: Propane_Tank_Monitor.A0, 10kΩ.Pin_0, Level_Meter.pin1
  N8: Propane_Tank_Monitor.A1, LPG_(Propane)_Sensor.A1, 10kΩ_2.leg1
  N9: 220Ω.Pin_1, Status.green_cathode
  N10: 220Ω_2.Pin_1, Status.blue_cathode
  N11: 220Ω_3.Pin_1, Status.red_cathode

custom parts:
  Arduino Shield PCB: Plain PCB Shaped to fit an Arduino "Shield"
